# Fritzing sketch joystick-lcd (saved by Fritzing 1.0.1rc)
breadboards: 1

parts:
  Componente1 = Arduino Uno (Rev3)
  R1 = Resistor [tolerance=±5% power=0.25W resistance=220 package=THT]
  R2 = Resistor [tolerance=±5% power=0.25W resistance=220 package=THT]
  R3 = Resistor [tolerance=±5% power=0.25W resistance=220 package=THT]
  LED1 = RGB LED (com. cathode, rgb) [color="Red (633nm)" current=0.030A package="5 mm [THT]"]
  Componente2 = Thumb Joystick
  Componente3 = LCD1602-I2C

nets:
  N1: Componente1.A0, Componente2.SEL
  N2: Componente1.A1, Componente2.HORZ
  N3: Componente1.A4/SDA, Componente3.SDA
  N4: Componente1.A5/SCL, Componente3.SCL
  N5: Componente1.D9_PWM, R3.Pin_1
  N6: Componente1.D10_PWM/SS, R1.Pin_1
  N7: Componente1.D11_PWM/MOSI, R2.Pin_1
  N8: Componente1.D2, Componente2.VERT
  VCC: Componente1.5V, Componente2.VCC, Componente3.VCC
  GND: Componente1.GND, LED1.red_anode, Componente2.GND, Componente3.GND
  N9: R1.Pin_0, LED1.green_anode
  N10: R2.Pin_0, LED1.common_cathode
  N11: R3.Pin_0, LED1.blue_anode

custom parts:
  LCD1602-I2C: A standard character display, usually with 2x16 characters. Comes in many colors with LCM1602 IIC attached.

// code stored in the sketch: joystick.ino
#define vermelho 11
#define verde 10
#define azul 9
#define x A0    // Saída analógica (Eixo X)
#define y A1    // Saída analógica (Eixo Y)
#define botao 2 // Saída digital do botão (Eixo Z)

void Vermelho()
{
    digitalWrite(azul, LOW);
    digitalWrite(verde, LOW);
    digitalWrite(vermelho, HIGH);
}
void Verde()
{
    digitalWrite(vermelho, LOW);
    digitalWrite(azul, LOW);
    digitalWrite(verde, HIGH);
}
void Azul()
{
    digitalWrite(vermelho, LOW);
    digitalWrite(verde, LOW);
    digitalWrite(azul, HIGH);
}
void Branco()
{
    digitalWrite(azul, HIGH);
    digitalWrite(vermelho, HIGH);
    digitalWrite(verde, HIGH);
}
void Magenta()
{
    digitalWrite(verde, LOW);
    digitalWrite(azul, HIGH);
    digitalWrite(vermelho, HIGH);
}
void Ciano()
{
    digitalWrite(vermelho, LOW);
    digitalWrite(verde, HIGH);
    digitalWrite(azul, HIGH);
}


void setup()
{
    Serial.begin(9600);
    while (!Serial)
        ;
    pinMode(vermelho, OUTPUT);
    pinMode(verde, OUTPUT);
    pinMode(azul, OUTPUT);
    pinMode(botao, INPUT_PULLUP); // HIGH quando o botão não estiver pressionado
}


void loop()
{
    // Notas:
    // > declarações switch...case não permitiram a leitura em 'tempo real' das
    // entradas analógicas, então declaraçóes 'if' (sem else if), foram as melhores

    if (analogRead(x) == 0)
    {
        Serial.println("direção: cima");
        Magenta();
    }
    if (analogRead(x) == 1023)
    {
        Serial.println("direção: baixo");
        Verde();
    }

    if (analogRead(y) == 0)
    {
        Serial.println("direção: direita");
        Azul();
    }
    if (analogRead(y) == 1023)
    {
        Serial.println("direção: esquerda");
        Vermelho();
    }

    if ((digitalRead(botao)) == 0)
    {
        Serial.println("botão pressionado");
        Ciano();
        delay(500);

        if ((digitalRead(botao)) == 0)
        {
            Branco();

            if ((digitalRead(botao)) == 0)
            {
                Serial.println("------------------------------------");
                Serial.print("Eixo X: ");
                Serial.println(analogRead(x));
                Serial.print("Eixo Y: ");
                Serial.println(analogRead(y));
                Serial.print("Leitura do botão: ");
                Serial.println(digitalRead(botao));
                Serial.println("------------------------------------");
            }
        }
    }


}
